// Logisim project PROJECT.circ as structural Verilog: 34 circuits, main circuit main
module main (
);

  wire ac_control_1_clr_ac, ac_control_1_inc_ac, ac_control_1_load_ac, ar_control_1_clr_ar,
       ar_control_1_inc_ar, ar_control_1_load_ar, bus_controller_1_s0, bus_controller_1_s1,
       bus_controller_1_s2, CLOCK, cout, dr_control_1_clr_dr, dr_control_1_inc_dr, dr_control_1_load_dr, E,
       FGI, FGO, I, IEN, ien_control_1_j_ien, ien_control_1_k_ien, ir_control_1_load_ir,
       pc_control_1_clear_pc, pc_control_1_inc_pc, pc_control_1_load_pc, R, r_control_1_j, r_control_1_k,
       read_and_write_1_read, read_and_write_1_write, S, time_and_control_1_i_2, tr_control_1_load_tr;
  wire [6:0] function_chooser_1_alu;
  wire [7:0] D, input_1_input, output_1_s2;
  wire [11:0] Address, ar_1_out_6, pc_1_out_6;
  wire [15:0] AC, alu_16_bit_1_answer, bus_1_output, DR, IR, ram_1_data, SC, tr_1_out_4;

  AR_control ar_control_1 (
    .clr_AR(ar_control_1_clr_ar), .load_AR(ar_control_1_load_ar), .inc_AR(ar_control_1_inc_ar), .SC(SC),
    .D(D), .R(R), .I(I));
  // Probe on bus_1_output
  AR ar_1 (
    .in_5(bus_1_output), .INCREMENT(ar_control_1_inc_ar), .LOAD(ar_control_1_load_ar),
    .clear(ar_control_1_clr_ar), .CLOCK(CLOCK), .out_6(ar_1_out_6));
  function_chooser function_chooser_1 (.addres(Address), .D(D), .I(I), .alu(function_chooser_1_alu), .SC(SC));
  // Probe on output_1_s2
  OUTPUT output_1 (.SC(SC), .in_3(bus_1_output), .Adress(Address), .D(D), .I(I), .clock(CLOCK), .S2(output_1_s2));
  // Probe on function_chooser_1_alu
  // Probe on input_1_input
  ALU_16_bit alu_16_bit_1 (
    .DR(DR), .CONTROLLER_LOAD_AC(function_chooser_1_alu), .INPUT(input_1_input), .E(E), .AC(AC),
    .answer(alu_16_bit_1_answer), .cout(cout));
  INPUT input_1 (.\input (input_1_input), .clock(CLOCK));
  Read_and_Write read_and_write_1 (.R(R), .SC(SC), .D(D), .write(read_and_write_1_write), .read(read_and_write_1_read));
  // Probe on SC
  AC_control ac_control_1 (
    .I(I), .addres(Address), .D(D), .load_AC(ac_control_1_load_ac), .clr_AC(ac_control_1_clr_ac),
    .inc_AC(ac_control_1_inc_ac), .SC(SC));
  TR_control tr_control_1 (.R(R), .SC(SC), .load_TR(tr_control_1_load_tr));
  // Probe on D
  PC pc_1 (
    .INPUT(bus_1_output), .out_6(pc_1_out_6), .LOAD(pc_control_1_load_pc), .INCREMENT(pc_control_1_inc_pc),
    .CLEAR(pc_control_1_clear_pc), .CLOCK(CLOCK));
  PC_control pc_control_1 (
    .R(R), .I(I), .FGO(FGO), .FGI(FGI), .E(E), .addres(Address), .load_pc(pc_control_1_load_pc),
    .clear_PC(pc_control_1_clear_pc), .inc_PC(pc_control_1_inc_pc), .SC(SC), .D(D), .AC(AC), .DC(DR));
  DR dr_1 (
    .out_6(DR), .in_1(bus_1_output), .LOAD(dr_control_1_load_dr), .INCREMENT(dr_control_1_inc_dr),
    .CLOCK(CLOCK), .clear(dr_control_1_clr_dr));
  DR_control dr_control_1 (
    .D(D), .load_DR(dr_control_1_load_dr), .inc_DR(dr_control_1_inc_dr), .clr_dr(dr_control_1_clr_dr), .SC(SC));
  AC ac_1 (
    .in_1(alu_16_bit_1_answer), .out_6(AC), .in_2(ac_control_1_load_ac), .in_5(ac_control_1_inc_ac),
    .in_3(ac_control_1_clr_ac), .in_4(CLOCK));
  IR ir_1 (.in_1(bus_1_output), .Load(ir_control_1_load_ir), .clock(CLOCK), .out_4(IR));
  IR_control ir_control_1 (.R(R), .in_2(SC), .load_IR(ir_control_1_load_ir));
  TR tr_1 (.in_1(bus_1_output), .out_4(tr_1_out_4), .in_3(CLOCK), .in_2(tr_control_1_load_tr));
  RAM #(.addrWidth(12), .dataWidth(16), .bus("separate")) ram_1 (
    .addr(ar_1_out_6), .din(bus_1_output), .data(ram_1_data), .str(read_and_write_1_write), .clk(CLOCK),
    .ld(read_and_write_1_read));  // open: sel, clr
  // Probe on ram_1_data
  // Probe on ar_1_out_6
  // Probe on pc_1_out_6
  // Probe on DR
  // Probe on AC
  // Probe on IR
  // Probe on tr_1_out_4
  BUS_CONTROLLER bus_controller_1 (
    .Adddress(Address), .SC(SC), .R(R), .I(I), .D(D), .S0(bus_controller_1_s0), .S1(bus_controller_1_s1),
    .S2(bus_controller_1_s2));
  BUS bus_1 (
    .Memory(ram_1_data), .AR(ar_1_out_6), .S2(bus_controller_1_s2), .PC(pc_1_out_6), .DR(DR), .AC(AC),
    .IR(IR), .TR(tr_1_out_4), .OUTPUT(bus_1_output), .S0(bus_controller_1_s0), .S1(bus_controller_1_s1));
  clock clock_1 (.S(S), .out_2(CLOCK));
  R_control r_control_1 (.FGO(FGO), .FGI(FGI), .IEN(IEN), .SC(SC), .R(R), .J(r_control_1_j), .K(r_control_1_k));
  IEN_control ien_control_1 (
    .I(I), .D(D), .R(R), .SC(SC), .Address(Address), .j_IEN(ien_control_1_j_ien), .K_IEN(ien_control_1_k_ien));
  R r_1 (.J(r_control_1_j), .clock(CLOCK), .k(r_control_1_k), .R(R));
  IEN ien_1 (.J(ien_control_1_j_ien), .clock(CLOCK), .k(ien_control_1_k_ien), .IEN(IEN));
  FGO fgo_1 (.I(I), .SC(SC), .Adddress(Address), .D(D), .FG0(FGO), .clock(CLOCK));
  Time_and_control time_and_control_1 (
    .Address(Address), .D(D), .SC(SC), .I_2(time_and_control_1_i_2), .IR(IR), .I(I), .R(R), .clock(CLOCK));
  S s_1 (.SC(SC), .I(I), .Address(Address), .D(D), .clock(CLOCK), .S(S));
  I i_1 (.R(R), .I(time_and_control_1_i_2), .SC(SC), .I_2(I), .clock(CLOCK));
  FGI fgi_1 (.I(I), .SC(SC), .Adress(Address), .D(D), .FGI(FGI), .in_3(CLOCK));
  E e_1 (.SC(SC), .Address(Address), .D(D), .cout(cout), .AC(AC), .E(E), .I(I), .clock(CLOCK));
endmodule

module FA_single_bit (
  input  c_i,
  input  A_i,
  input  B_i,
  output ANS,
  output c_i_1
);

  wire and_1_out, and_2_out, xor_1_out;

  xor xor_1 (xor_1_out, A_i, B_i);
  and and_1 (and_1_out, A_i, B_i);
  xor xor_2 (ANS, c_i, xor_1_out);
  and and_2 (and_2_out, c_i, xor_1_out);
  or or_1 (c_i_1, and_2_out, and_1_out);
endmodule

module ALU_16_bit (
  input  [15:0] DR,
  input  [15:0] AC,
  input  [6:0] CONTROLLER_LOAD_AC,
  input  [7:0] INPUT,
  input  E,
  output [15:0] answer,
  output cout
);

  wire alu_1_bit_1_c_i_1, alu_1_bit_2_c_i_1, alu_1_bit_3_c_i_1, alu_1_bit_4_c_i_1, alu_1_bit_5_c_i_1,
       alu_1_bit_6_c_i_1, alu_1_bit_7_c_i_1, alu_1_bit_8_c_i_1, alu_1_bit_9_c_i_1, alu_1_bit_10_c_i_1,
       alu_1_bit_11_c_i_1, alu_1_bit_12_c_i_1, alu_1_bit_13_c_i_1, alu_1_bit_14_c_i_1, c_8;

  ALU_1_bit alu_1_bit_1 (
    .CONTROLLER(CONTROLLER_LOAD_AC), .input_i(INPUT[0]), .AC_i_1(AC[1]), .AC_i_1_2(E), .C_i(1'b0),
    .DR_i(DR[0]), .AC_i(AC[0]), .c_i_1(alu_1_bit_1_c_i_1), .ALU_i(answer[0]));
  ALU_1_bit alu_1_bit_2 (
    .CONTROLLER(CONTROLLER_LOAD_AC), .input_i(1'b0), .AC_i_1(AC[9]), .AC_i_1_2(AC[7]), .C_i(c_8),
    .DR_i(DR[8]), .AC_i(AC[8]), .c_i_1(alu_1_bit_2_c_i_1), .ALU_i(answer[8]));
  ALU_1_bit alu_1_bit_3 (
    .CONTROLLER(CONTROLLER_LOAD_AC), .input_i(INPUT[1]), .AC_i_1(AC[2]), .AC_i_1_2(AC[0]),
    .C_i(alu_1_bit_1_c_i_1), .DR_i(DR[1]), .AC_i(AC[1]), .c_i_1(alu_1_bit_3_c_i_1), .ALU_i(answer[1]));
  ALU_1_bit alu_1_bit_4 (
    .CONTROLLER(CONTROLLER_LOAD_AC), .input_i(1'b0), .AC_i_1(AC[10]), .AC_i_1_2(AC[8]),
    .C_i(alu_1_bit_2_c_i_1), .DR_i(DR[9]), .AC_i(AC[9]), .c_i_1(alu_1_bit_4_c_i_1), .ALU_i(answer[9]));
  ALU_1_bit alu_1_bit_5 (
    .CONTROLLER(CONTROLLER_LOAD_AC), .input_i(INPUT[2]), .AC_i_1(AC[3]), .AC_i_1_2(AC[1]),
    .C_i(alu_1_bit_3_c_i_1), .DR_i(DR[2]), .AC_i(AC[2]), .c_i_1(alu_1_bit_5_c_i_1), .ALU_i(answer[2]));
  ALU_1_bit alu_1_bit_6 (
    .CONTROLLER(CONTROLLER_LOAD_AC), .input_i(1'b0), .AC_i_1(AC[11]), .AC_i_1_2(AC[9]),
    .C_i(alu_1_bit_4_c_i_1), .DR_i(DR[10]), .AC_i(AC[10]), .c_i_1(alu_1_bit_6_c_i_1), .ALU_i(answer[10]));
  ALU_1_bit alu_1_bit_7 (
    .CONTROLLER(CONTROLLER_LOAD_AC), .input_i(INPUT[3]), .AC_i_1(AC[4]), .AC_i_1_2(AC[2]),
    .C_i(alu_1_bit_5_c_i_1), .DR_i(DR[3]), .AC_i(AC[3]), .c_i_1(alu_1_bit_7_c_i_1), .ALU_i(answer[3]));
  ALU_1_bit alu_1_bit_8 (
    .CONTROLLER(CONTROLLER_LOAD_AC), .input_i(1'b0), .AC_i_1(AC[12]), .AC_i_1_2(AC[10]),
    .C_i(alu_1_bit_6_c_i_1), .DR_i(DR[11]), .AC_i(AC[11]), .c_i_1(alu_1_bit_8_c_i_1), .ALU_i(answer[11]));
  ALU_1_bit alu_1_bit_9 (
    .CONTROLLER(CONTROLLER_LOAD_AC), .input_i(INPUT[4]), .AC_i_1(AC[5]), .AC_i_1_2(AC[3]),
    .C_i(alu_1_bit_7_c_i_1), .DR_i(DR[4]), .AC_i(AC[4]), .c_i_1(alu_1_bit_9_c_i_1), .ALU_i(answer[4]));
  ALU_1_bit alu_1_bit_10 (
    .CONTROLLER(CONTROLLER_LOAD_AC), .input_i(1'b0), .AC_i_1(AC[13]), .AC_i_1_2(AC[11]),
    .C_i(alu_1_bit_8_c_i_1), .DR_i(DR[12]), .AC_i(AC[12]), .c_i_1(alu_1_bit_10_c_i_1), .ALU_i(answer[12]));
  ALU_1_bit alu_1_bit_11 (
    .CONTROLLER(CONTROLLER_LOAD_AC), .input_i(INPUT[5]), .AC_i_1(AC[6]), .AC_i_1_2(AC[4]),
    .C_i(alu_1_bit_9_c_i_1), .DR_i(DR[5]), .AC_i(AC[5]), .c_i_1(alu_1_bit_11_c_i_1), .ALU_i(answer[5]));
  ALU_1_bit alu_1_bit_12 (
    .CONTROLLER(CONTROLLER_LOAD_AC), .input_i(1'b0), .AC_i_1(AC[14]), .AC_i_1_2(AC[12]),
    .C_i(alu_1_bit_10_c_i_1), .DR_i(DR[13]), .AC_i(AC[13]), .c_i_1(alu_1_bit_12_c_i_1), .ALU_i(answer[13]));
  ALU_1_bit alu_1_bit_13 (
    .CONTROLLER(CONTROLLER_LOAD_AC), .input_i(INPUT[6]), .AC_i_1(AC[7]), .AC_i_1_2(AC[5]),
    .C_i(alu_1_bit_11_c_i_1), .DR_i(DR[6]), .AC_i(AC[6]), .c_i_1(alu_1_bit_13_c_i_1), .ALU_i(answer[6]));
  ALU_1_bit alu_1_bit_14 (
    .CONTROLLER(CONTROLLER_LOAD_AC), .input_i(1'b0), .AC_i_1(AC[15]), .AC_i_1_2(AC[13]),
    .C_i(alu_1_bit_12_c_i_1), .DR_i(DR[14]), .AC_i(AC[14]), .c_i_1(alu_1_bit_14_c_i_1), .ALU_i(answer[14]));
  ALU_1_bit alu_1_bit_15 (
    .CONTROLLER(CONTROLLER_LOAD_AC), .input_i(INPUT[7]), .AC_i_1(AC[8]), .AC_i_1_2(AC[6]),
    .C_i(alu_1_bit_13_c_i_1), .DR_i(DR[7]), .AC_i(AC[7]), .c_i_1(c_8), .ALU_i(answer[7]));
  ALU_1_bit alu_1_bit_16 (
    .CONTROLLER(CONTROLLER_LOAD_AC), .input_i(1'b0), .AC_i_1(E), .AC_i_1_2(AC[14]), .C_i(alu_1_bit_14_c_i_1),
    .DR_i(DR[15]), .AC_i(AC[15]), .c_i_1(cout), .ALU_i(answer[15]));

  // Other names for the same wires on the sheet: AC_LOW[7:0] = AC[7:0]; bit7 = AC[7]; AC_HIGH[7:0] = AC[15:8];
  //   bit8 = AC[8]; DR_HIGH[7:0] = DR[15:8]
endmodule

module ALU_1_bit (
  input  C_i,
  input  DR_i,
  input  AC_i,
  input  [6:0] CONTROLLER,
  input  input_i,
  input  AC_i_1,
  input  AC_i_1_2,
  output c_i_1,
  output ALU_i
);

  wire ADD_out, AND_out, COM_out, DR_out, fa_single_bit_1_ans, INP_out, not_1_out, SHL_out, SHR_out;

  FA_single_bit fa_single_bit_1 (.c_i(C_i), .A_i(AC_i), .B_i(DR_i), .ANS(fa_single_bit_1_ans), .c_i_1(c_i_1));
  not not_1 (not_1_out, AC_i);
  and AND (AND_out, CONTROLLER[0], AC_i, DR_i);
  and ADD (ADD_out, fa_single_bit_1_ans, CONTROLLER[1]);
  and DR (DR_out, CONTROLLER[2], DR_i);
  and INP (INP_out, CONTROLLER[3], input_i);
  and COM (COM_out, CONTROLLER[4], not_1_out);
  and SHR (SHR_out, CONTROLLER[5], AC_i_1);
  and SHL (SHL_out, CONTROLLER[6], AC_i_1_2);
  or or_1 (ALU_i, AND_out, ADD_out, DR_out, INP_out, COM_out, SHR_out, SHL_out);
endmodule

// CONTROL
module Time_and_control (
  input  [15:0] IR,
  input  I,
  input  R,
  input  clock,
  output [11:0] Address,
  output [7:0] D,
  output I_2,
  output [15:0] SC
);

  wire [3:0] counter_1_out_6;

  Decoder #(.select(3), .enable("false")) decoder_1 (
    .out0(D[0]), .out1(D[1]), .out2(D[2]), .out3(D[3]), .out4(D[4]), .out5(D[5]), .out6(D[6]), .out7(D[7]),
    .sel(IR[14:12]));
  COUNTER counter_1 (.I(I), .R(R), .SC(SC), .D(D), .clock(clock), .out_6(counter_1_out_6));
  Decoder #(.select(4)) decoder_2 (
    .out0(SC[0]), .out1(SC[1]), .out2(SC[2]), .out3(SC[3]), .out4(SC[4]), .out5(SC[5]), .out6(SC[6]),
    .out7(SC[7]), .out8(SC[8]), .out9(SC[9]), .out10(SC[10]), .out11(SC[11]), .out12(SC[12]), .out13(SC[13]),
    .out14(SC[14]), .out15(SC[15]), .sel(counter_1_out_6));  // open: en
  // Probe on counter_1_out_6

  assign Address = IR[11:0];
  assign I_2 = IR[15];
endmodule

module clock (
  input  S,
  output out_2
);

  wire clock_1_out, not_1_out;

  Clock clock_1 (.out(clock_1_out));
  not not_1 (not_1_out, S);
  and and_1 (out_2, clock_1_out, not_1_out);
endmodule

module AR (
  input  INCREMENT,
  input  LOAD,
  input  clear,
  input  CLOCK,
  input  [15:0] in_5,
  output [11:0] out_6
);

  wire fa_single_bit_1_c_i_1, fa_single_bit_2_c_i_1, fa_single_bit_3_c_i_1, fa_single_bit_4_c_i_1,
       fa_single_bit_5_c_i_1, fa_single_bit_6_c_i_1, fa_single_bit_7_c_i_1, fa_single_bit_8_c_i_1,
       fa_single_bit_9_c_i_1, fa_single_bit_10_c_i_1, fa_single_bit_11_c_i_1, or_2_out;
  wire [11:0] and_1_out, and_2_out, or_1_out, PLUSONE;

  assign and_1_out = in_5[11:0] & {12{LOAD}};  // AND_Gate and_1, 12 bits wide
  // Probe on and_1_out
  assign and_2_out = {12{INCREMENT}} & PLUSONE;  // AND_Gate and_2, 12 bits wide
  assign or_1_out = and_1_out | and_2_out;  // OR_Gate or_1, 12 bits wide
  // Probe on {12{LOAD}}
  or or_2 (or_2_out, INCREMENT, LOAD);
  Register #(.width(12), .trigger("falling")) register_1 (
    .D(or_1_out), .en(or_2_out), .Q(out_6), .clk(CLOCK), .clr(clear));
  FA_single_bit fa_single_bit_1 (
    .c_i(1'b0), .A_i(INCREMENT), .B_i(out_6[0]), .ANS(PLUSONE[0]), .c_i_1(fa_single_bit_1_c_i_1));
  FA_single_bit fa_single_bit_2 (
    .c_i(1'b0), .A_i(fa_single_bit_1_c_i_1), .B_i(out_6[1]), .ANS(PLUSONE[1]), .c_i_1(fa_single_bit_2_c_i_1));
  FA_single_bit fa_single_bit_3 (
    .c_i(1'b0), .A_i(fa_single_bit_2_c_i_1), .B_i(out_6[2]), .ANS(PLUSONE[2]), .c_i_1(fa_single_bit_3_c_i_1));
  FA_single_bit fa_single_bit_4 (
    .c_i(1'b0), .A_i(fa_single_bit_3_c_i_1), .B_i(out_6[3]), .ANS(PLUSONE[3]), .c_i_1(fa_single_bit_4_c_i_1));
  FA_single_bit fa_single_bit_5 (
    .c_i(1'b0), .A_i(fa_single_bit_4_c_i_1), .B_i(out_6[4]), .ANS(PLUSONE[4]), .c_i_1(fa_single_bit_5_c_i_1));
  FA_single_bit fa_single_bit_6 (
    .c_i(1'b0), .A_i(fa_single_bit_5_c_i_1), .B_i(out_6[5]), .ANS(PLUSONE[5]), .c_i_1(fa_single_bit_6_c_i_1));
  FA_single_bit fa_single_bit_7 (
    .c_i(1'b0), .A_i(fa_single_bit_6_c_i_1), .B_i(out_6[6]), .ANS(PLUSONE[6]), .c_i_1(fa_single_bit_7_c_i_1));
  FA_single_bit fa_single_bit_8 (
    .c_i(1'b0), .A_i(fa_single_bit_7_c_i_1), .B_i(out_6[7]), .ANS(PLUSONE[7]), .c_i_1(fa_single_bit_8_c_i_1));
  FA_single_bit fa_single_bit_9 (
    .c_i(1'b0), .A_i(fa_single_bit_8_c_i_1), .B_i(out_6[8]), .ANS(PLUSONE[8]), .c_i_1(fa_single_bit_9_c_i_1));
  FA_single_bit fa_single_bit_10 (
    .c_i(1'b0), .A_i(fa_single_bit_9_c_i_1), .B_i(out_6[9]), .ANS(PLUSONE[9]), .c_i_1(fa_single_bit_10_c_i_1));
  FA_single_bit fa_single_bit_11 (
    .c_i(1'b0), .A_i(fa_single_bit_10_c_i_1), .B_i(out_6[10]), .ANS(PLUSONE[10]),
    .c_i_1(fa_single_bit_11_c_i_1));
  FA_single_bit fa_single_bit_12 (
    .c_i(1'b0), .A_i(fa_single_bit_11_c_i_1), .B_i(out_6[11]), .ANS(PLUSONE[11]));  // open: c_i_1

  // Other names for the same wires on the sheet: INC = INCREMENT; INPUT[11:0] = in_5[11:0]; LD[11:0] = {12{LOAD}}
endmodule

// AR_cntrl
module AR_control (
  input  [7:0] D,
  input  R,
  input  [15:0] SC,
  input  I,
  output clr_AR,
  output load_AR,
  output inc_AR
);

  wire and_3_out, and_4_out, and_5_out, not_1_out, not_2_out;

  and and_1 (inc_AR, SC[4], D[5]);
  and and_2 (clr_AR, SC[0], R);
  not not_1 (not_1_out, R);
  not not_2 (not_2_out, D[7]);
  and and_3 (and_3_out, not_1_out, SC[0]);
  and and_4 (and_4_out, not_1_out, SC[2]);
  and and_5 (and_5_out, not_2_out, I, SC[3]);
  or or_1 (load_AR, and_3_out, and_4_out, and_5_out);
endmodule

module PC (
  input  [15:0] INPUT,
  input  INCREMENT,
  input  LOAD,
  input  CLEAR,
  input  CLOCK,
  output [11:0] out_6
);

  AR ar_1 (.in_5(INPUT), .INCREMENT(INCREMENT), .LOAD(LOAD), .clear(CLEAR), .CLOCK(CLOCK), .out_6(out_6));
endmodule

// PC_cntrl
module PC_control (
  input  R,
  input  I,
  input  FGO,
  input  FGI,
  input  [7:0] D,
  input  E,
  input  [11:0] addres,
  input  [15:0] SC,
  input  [15:0] DC,
  input  [15:0] AC,
  output load_pc,
  output clear_PC,
  output inc_PC
);

  wire AC0, and_2_out, and_3_out, and_6_out, and_7_out, and_8_out, and_9_out, and_12_out, and_13_out,
       and_14_out, and_15_out, inc_1, inc_2, inc_3, nor_2_out, not_1_out, not_2_out, not_3_out, not_4_out,
       or_2_out, or_4_out, p, small_r;

  nor nor_1 (AC0, AC[0], AC[1], AC[2], AC[3], AC[4], AC[5], AC[6], AC[7], AC[9], AC[10], AC[11], AC[12], AC[13], AC[14], AC[15], AC[8]);
  and and_1 (clear_PC, R, SC[1]);
  and and_2 (and_2_out, D[4], SC[4]);
  and and_3 (and_3_out, D[5], SC[5]);
  or or_1 (load_pc, and_2_out, and_3_out);
  nor nor_2 (nor_2_out, DC[0], DC[1], DC[2], DC[3], DC[4], DC[5], DC[6], DC[7], DC[9], DC[10], DC[11], DC[12], DC[13], DC[14], DC[15], DC[8]);
  and and_4 (p, I, D[7], SC[3]);
  not not_1 (not_1_out, R);
  not not_2 (not_2_out, I);
  and and_5 (small_r, not_2_out, D[7], SC[3]);
  and and_6 (and_6_out, FGI, addres[9]);
  and and_7 (and_7_out, addres[8], FGO);
  and and_8 (and_8_out, SC[1], not_1_out);
  and and_9 (and_9_out, SC[2], R);
  and and_10 (inc_1, SC[6], nor_2_out, D[6]);
  or or_2 (or_2_out, and_6_out, and_7_out);
  and and_11 (inc_3, or_2_out, p);
  or or_3 (inc_PC, and_8_out, and_9_out, inc_1, inc_2, inc_3);
  not not_3 (not_3_out, E);
  and and_12 (and_12_out, not_3_out, addres[1]);
  and and_13 (and_13_out, addres[2], AC0);
  and and_14 (and_14_out, addres[3], AC[15]);
  not not_4 (not_4_out, AC[15]);
  and and_15 (and_15_out, not_4_out, addres[4]);
  or or_4 (or_4_out, and_12_out, and_13_out, and_14_out, and_15_out);
  and and_16 (inc_2, or_4_out, small_r);

  // Other names for the same wires on the sheet: AC_15 = AC[15]; B1 = addres[1]; B2 = addres[2]; B3 = addres[3];
  //   B4 = addres[4]; B8 = addres[8]; B9 = addres[9]; T1 = SC[1]; T2 = SC[2]; T3 = SC[3]; T4 = SC[4]; T5 = SC[5];
  //   T6 = SC[6]
endmodule

module DR (
  input  [15:0] in_1,
  input  INCREMENT,
  input  LOAD,
  input  CLOCK,
  input  clear,
  output [15:0] out_6
);

  wire fa_single_bit_1_c_i_1, fa_single_bit_2_c_i_1, fa_single_bit_3_c_i_1, fa_single_bit_4_c_i_1,
       fa_single_bit_5_c_i_1, fa_single_bit_6_c_i_1, fa_single_bit_7_c_i_1, fa_single_bit_8_c_i_1,
       fa_single_bit_9_c_i_1, fa_single_bit_10_c_i_1, fa_single_bit_11_c_i_1, fa_single_bit_12_c_i_1,
       fa_single_bit_13_c_i_1, fa_single_bit_14_c_i_1, fa_single_bit_15_c_i_1, or_2_out;
  wire [15:0] and_1_out, and_2_out, or_1_out, plus_one;

  assign and_1_out = in_1 & {16{LOAD}};  // AND_Gate and_1, 16 bits wide
  // Probe on and_1_out
  assign and_2_out = {16{INCREMENT}} & plus_one;  // AND_Gate and_2, 16 bits wide
  assign or_1_out = and_1_out | and_2_out;  // OR_Gate or_1, 16 bits wide
  // Probe on {16{LOAD}}
  or or_2 (or_2_out, INCREMENT, LOAD);
  Register #(.width(16), .trigger("falling")) register_1 (
    .D(or_1_out), .en(or_2_out), .Q(out_6), .clk(CLOCK), .clr(clear));
  FA_single_bit fa_single_bit_1 (
    .c_i(1'b0), .A_i(INCREMENT), .B_i(out_6[0]), .ANS(plus_one[0]), .c_i_1(fa_single_bit_1_c_i_1));
  FA_single_bit fa_single_bit_2 (
    .c_i(1'b0), .A_i(fa_single_bit_1_c_i_1), .B_i(out_6[1]), .ANS(plus_one[1]), .c_i_1(fa_single_bit_2_c_i_1));
  FA_single_bit fa_single_bit_3 (
    .c_i(1'b0), .A_i(fa_single_bit_2_c_i_1), .B_i(out_6[2]), .ANS(plus_one[2]), .c_i_1(fa_single_bit_3_c_i_1));
  FA_single_bit fa_single_bit_4 (
    .c_i(1'b0), .A_i(fa_single_bit_3_c_i_1), .B_i(out_6[3]), .ANS(plus_one[3]), .c_i_1(fa_single_bit_4_c_i_1));
  FA_single_bit fa_single_bit_5 (
    .c_i(1'b0), .A_i(fa_single_bit_4_c_i_1), .B_i(out_6[4]), .ANS(plus_one[4]), .c_i_1(fa_single_bit_5_c_i_1));
  FA_single_bit fa_single_bit_6 (
    .c_i(1'b0), .A_i(fa_single_bit_5_c_i_1), .B_i(out_6[5]), .ANS(plus_one[5]), .c_i_1(fa_single_bit_6_c_i_1));
  FA_single_bit fa_single_bit_7 (
    .c_i(1'b0), .A_i(fa_single_bit_6_c_i_1), .B_i(out_6[6]), .ANS(plus_one[6]), .c_i_1(fa_single_bit_7_c_i_1));
  FA_single_bit fa_single_bit_8 (
    .c_i(1'b0), .A_i(fa_single_bit_7_c_i_1), .B_i(out_6[7]), .ANS(plus_one[7]), .c_i_1(fa_single_bit_8_c_i_1));
  FA_single_bit fa_single_bit_9 (
    .c_i(1'b0), .A_i(fa_single_bit_8_c_i_1), .B_i(out_6[8]), .ANS(plus_one[8]), .c_i_1(fa_single_bit_9_c_i_1));
  FA_single_bit fa_single_bit_10 (
    .c_i(1'b0), .A_i(fa_single_bit_9_c_i_1), .B_i(out_6[9]), .ANS(plus_one[9]), .c_i_1(fa_single_bit_10_c_i_1));
  FA_single_bit fa_single_bit_11 (
    .c_i(1'b0), .A_i(fa_single_bit_10_c_i_1), .B_i(out_6[10]), .ANS(plus_one[10]),
    .c_i_1(fa_single_bit_11_c_i_1));
  FA_single_bit fa_single_bit_12 (
    .c_i(1'b0), .A_i(fa_single_bit_11_c_i_1), .B_i(out_6[11]), .ANS(plus_one[11]),
    .c_i_1(fa_single_bit_12_c_i_1));
  FA_single_bit fa_single_bit_13 (
    .c_i(1'b0), .A_i(fa_single_bit_12_c_i_1), .B_i(out_6[12]), .ANS(plus_one[12]),
    .c_i_1(fa_single_bit_13_c_i_1));
  FA_single_bit fa_single_bit_14 (
    .c_i(1'b0), .A_i(fa_single_bit_13_c_i_1), .B_i(out_6[13]), .ANS(plus_one[13]),
    .c_i_1(fa_single_bit_14_c_i_1));
  FA_single_bit fa_single_bit_15 (
    .c_i(1'b0), .A_i(fa_single_bit_14_c_i_1), .B_i(out_6[14]), .ANS(plus_one[14]),
    .c_i_1(fa_single_bit_15_c_i_1));
  FA_single_bit fa_single_bit_16 (
    .c_i(1'b0), .A_i(fa_single_bit_15_c_i_1), .B_i(out_6[15]), .ANS(plus_one[15]));  // open: c_i_1

  // Other names for the same wires on the sheet: INC = INCREMENT; LD[15:0] = {16{LOAD}}
endmodule

// DR_cntrl
module DR_control (
  input  [7:0] D,
  input  [15:0] SC,
  output load_DR,
  output inc_DR,
  output clr_dr
);

  wire or_1_out;

  or or_1 (or_1_out, D[0], D[1], D[2], D[6]);
  and and_1 (load_DR, or_1_out, SC[4]);
  and and_2 (inc_DR, D[6], SC[5]);

  assign clr_dr = 1'b0;

  // Other names for the same wires on the sheet: T4 = SC[4]
endmodule

module IR (
  input  [15:0] in_1,
  input  Load,
  input  clock,
  output [15:0] out_4
);

  Register #(.width(16), .trigger("falling")) register_1 (.D(in_1), .en(Load), .Q(out_4), .clk(clock));  // open: clr
endmodule

module IR_control (
  input  R,
  input  [15:0] in_2,
  output load_IR
);

  wire not_1_out;

  not not_1 (not_1_out, R);
  and and_1 (load_IR, not_1_out, in_2[1]);
endmodule

module TR (
  input  [15:0] in_1,
  input  in_2,
  input  in_3,
  output [15:0] out_4
);

  DR dr_1 (.out_6(out_4), .in_1(in_1), .LOAD(in_2), .INCREMENT(1'b0), .CLOCK(in_3), .clear(1'b0));
endmodule

module TR_control (
  input  R,
  input  [15:0] SC,
  output load_TR
);

  and and_1 (load_TR, R, SC[0]);
endmodule

module AC (
  input  [15:0] in_1,
  input  in_2,
  input  in_3,
  input  in_4,
  input  in_5,
  output [15:0] out_6
);

  DR dr_1 (.out_6(out_6), .in_1(in_1), .LOAD(in_2), .INCREMENT(in_5), .CLOCK(in_4), .clear(in_3));
endmodule

// AC_cntrl
module AC_control (
  input  [11:0] addres,
  input  [7:0] D,
  input  I,
  input  [15:0] SC,
  output load_AC,
  output clr_AC,
  output inc_AC
);

  wire and_1_out, and_2_out, and_3_out, not_1_out, or_1_out, or_2_out, p, r;

  or or_1 (or_1_out, addres[6], addres[7], addres[9]);
  or or_2 (or_2_out, D[0], D[1], D[2]);
  and and_1 (and_1_out, or_1_out, r);
  and and_2 (and_2_out, addres[11], p);
  and and_3 (and_3_out, or_2_out, SC[5]);
  or or_3 (load_AC, and_1_out, and_2_out, and_3_out);
  not not_1 (not_1_out, I);
  and and_4 (r, not_1_out, D[7], SC[3]);
  and and_5 (p, I, D[7], SC[3]);
  and and_6 (clr_AC, addres[11], r);
  and and_7 (inc_AC, addres[5], r);

  // Other names for the same wires on the sheet: B5 = addres[5]; B11 = addres[11]; T3 = SC[3]; T5 = SC[5]
endmodule

module IEN (
  input  J,
  input  clock,
  input  k,
  output IEN
);

  J_K_Flip_Flop #(.trigger("falling")) j_k_ff_1 (.J(J), .clk(clock), .K(k), .Q(IEN));  // open: Qn, preset, en, reset
endmodule

module IEN_control (
  input  [11:0] Address,
  input  I,
  input  [7:0] D,
  input  R,
  input  [15:0] SC,
  output j_IEN,
  output K_IEN
);

  wire and_3_out, and_4_out, P;

  and and_1 (P, I, SC[3], D[7]);
  and and_2 (j_IEN, P, Address[7]);
  and and_3 (and_3_out, P, Address[6]);
  and and_4 (and_4_out, R, SC[2]);
  or or_1 (K_IEN, and_3_out, and_4_out);

  // Other names for the same wires on the sheet: B6 = Address[6]; B7 = Address[7]; T2 = SC[2]; T3 = SC[3]
endmodule

module R (
  input  J,
  input  clock,
  input  k,
  output R
);

  J_K_Flip_Flop #(.trigger("falling")) j_k_ff_1 (.J(J), .clk(clock), .K(k), .Q(R));  // open: Qn, preset, en, reset
endmodule

module R_control (
  input  FGO,
  input  FGI,
  input  IEN,
  input  [15:0] SC,
  input  R,
  output J,
  output K
);

  wire nor_1_out, or_1_out;

  nor nor_1 (nor_1_out, SC[0], SC[1], SC[2]);
  or or_1 (or_1_out, FGO, FGI);
  and and_1 (J, or_1_out, nor_1_out, IEN);
  and and_2 (K, SC[2], R);
endmodule

module FGI (
  input  I,
  input  [15:0] SC,
  input  in_3,
  input  [11:0] Adress,
  input  [7:0] D,
  output FGI
);

  wire and_1_out, nand_1_out, p;

  nand nand_1 (nand_1_out, p, Adress[11]);
  and and_1 (and_1_out, FGI, nand_1_out);
  D_Flip_Flop #(.trigger("falling")) d_ff_1 (.clk(in_3), .D(and_1_out), .Q(FGI));  // open: Qn, preset, en, reset
  and and_2 (p, I, D[7], SC[3]);

  // Other names for the same wires on the sheet: B11 = Adress[11]; T3 = SC[3]
endmodule

module FGO (
  input  I,
  input  [15:0] SC,
  input  clock,
  input  [11:0] Adddress,
  input  [7:0] D,
  output FG0
);

  wire and_1_out, nand_1_out, p;

  nand nand_1 (nand_1_out, p, Adddress[10]);
  and and_1 (and_1_out, FG0, nand_1_out);
  D_Flip_Flop #(.trigger("falling")) d_ff_1 (.clk(clock), .D(and_1_out), .Q(FG0));  // open: Qn, preset, en, reset
  and and_2 (p, I, D[7], SC[3]);

  // Other names for the same wires on the sheet: B10 = Adddress[10]; T3 = SC[3]
endmodule

module I (
  input  R,
  input  clock,
  input  I,
  input  [15:0] SC,
  output I_2
);

  wire and_1_out, and_2_out, and_3_out, not_2_out, or_1_out, R_prime;

  not not_1 (R_prime, R);
  and and_1 (and_1_out, R_prime, SC[2]);
  and and_2 (and_2_out, I_2, not_2_out);
  not not_2 (not_2_out, and_1_out);
  and and_3 (and_3_out, and_1_out, I);
  or or_1 (or_1_out, and_2_out, and_3_out);
  D_Flip_Flop #(.trigger("falling")) d_ff_1 (.clk(clock), .D(or_1_out), .Q(I_2));  // open: Qn, preset, en, reset

  // Other names for the same wires on the sheet: T2 = SC[2]
endmodule

module S (
  input  [15:0] SC,
  input  clock,
  input  I,
  input  [11:0] Address,
  input  [7:0] D,
  output S
);

  wire and_1_out, not_1_out;

  not not_1 (not_1_out, I);
  and and_1 (and_1_out, Address[0], SC[3], D[7], not_1_out);
  T_Flip_Flop t_ff_1 (.clk(clock), .T(and_1_out), .Q(S));  // open: Qn, preset, reset, en

  // Other names for the same wires on the sheet: B0 = Address[0]; T3 = SC[3]
endmodule

module E (
  input  I,
  input  [15:0] SC,
  input  [11:0] Address,
  input  clock,
  input  [7:0] D,
  input  cout,
  input  [15:0] AC,
  output E
);

  wire and_1_out, and_2_out, and_3_out, and_4_out, and_5_out, and_6_out, nand_1_out, nand_2_out, nand_3_out,
       nand_4_out, nand_5_out, not_1_out, not_2_out, or_1_out, or_2_out, r;

  not not_1 (not_1_out, E);
  nand nand_1 (nand_1_out, r, Address[10]);
  nand nand_2 (nand_2_out, SC[5], D[1]);
  nand nand_3 (nand_3_out, r, Address[8]);
  nand nand_4 (nand_4_out, r, Address[7]);
  nand nand_5 (nand_5_out, r, Address[6]);
  and and_1 (and_1_out, r, 1'b0, Address[10]);
  and and_2 (and_2_out, SC[5], D[1], cout);
  and and_3 (and_3_out, not_1_out, r, Address[8]);
  and and_4 (and_4_out, AC[0], r, Address[7]);
  and and_5 (and_5_out, AC[15], r, Address[6]);
  and and_6 (and_6_out, E, nand_1_out, nand_2_out, nand_3_out, nand_4_out, nand_5_out);
  or or_1 (or_1_out, and_1_out, and_2_out, and_3_out, and_4_out, and_5_out);
  or or_2 (or_2_out, and_6_out, or_1_out);
  not not_2 (not_2_out, I);
  and and_7 (r, not_2_out, D[7], SC[3]);
  D_Flip_Flop #(.trigger("falling")) d_ff_1 (.clk(clock), .D(or_2_out), .Q(E));  // open: Qn, preset, en, reset

  // Other names for the same wires on the sheet: AC_0 = AC[0]; AC_15 = AC[15]; B6 = Address[6]; B7 = Address[7];
  //   B8 = Address[8]; B10 = Address[10]; T3 = SC[3]; T5 = SC[5]
endmodule

module function_chooser (
  input  [11:0] addres,
  input  [7:0] D,
  input  I,
  input  [15:0] SC,
  output [6:0] alu
);

  wire not_1_out, p, r;

  and and_1 (alu[0], D[0], SC[5]);
  and and_2 (alu[1], SC[5], D[1]);
  and and_3 (alu[2], D[2], SC[5]);
  and and_4 (alu[3], p, addres[11]);
  and and_5 (alu[4], r, addres[9]);
  and and_6 (alu[5], addres[7], r);
  and and_7 (alu[6], addres[6], r);
  and and_8 (p, I, D[7], SC[3]);
  not not_1 (not_1_out, I);
  and and_9 (r, not_1_out, D[7], SC[3]);

  // Other names for the same wires on the sheet: B5 = addres[5]; B6 = addres[6]; B7 = addres[7]; B9 = addres[9];
  //   B11 = addres[11]; T3 = SC[3]; T5 = SC[5]
endmodule

module INPUT (
  input  clock,
  output [7:0] \input 
);

  Register #(.trigger("falling")) register_1 (.Q(\input ), .clk(clock));  // open: D, en, clr
endmodule

module OUTPUT (
  input  I,
  input  [15:0] SC,
  input  [15:0] in_3,
  input  [11:0] Adress,
  input  clock,
  input  [7:0] D,
  output [7:0] S2
);

  wire and_2_out, p;

  and and_1 (p, I, D[7], SC[3]);
  and and_2 (and_2_out, Adress[10], p);
  Register #(.trigger("falling")) register_1 (.D(in_3[7:0]), .en(and_2_out), .Q(S2), .clk(clock));  // open: clr

  // Other names for the same wires on the sheet: B10 = Adress[10]; T3 = SC[3]
endmodule

module COUNTER (
  input  clock,
  input  I,
  input  R,
  input  [15:0] SC,
  input  [7:0] D,
  output [3:0] out_6
);

  wire and_3_out, and_4_out, and_5_out, and_6_out, and_7_out, and_8_out, and_9_out, and_10_out, load,
       not_1_out, not_2_out, p, r_t;

  Counter #(.width(4), .max('hf), .trigger("falling")) counter_1 (
    .load(load), .D(4'b0000), .count(not_1_out), .Q(out_6), .clk(clock));  // open: carry, clr
  not not_1 (not_1_out, load);
  and and_1 (p, I, D[7], SC[3]);
  not not_2 (not_2_out, I);
  and and_2 (r_t, not_2_out, D[7], SC[3]);
  and and_3 (and_3_out, R, SC[2]);
  and and_4 (and_4_out, D[0], SC[5]);
  and and_5 (and_5_out, D[1], SC[5]);
  and and_6 (and_6_out, D[2], SC[5]);
  and and_7 (and_7_out, D[3], SC[4]);
  and and_8 (and_8_out, D[4], SC[4]);
  and and_9 (and_9_out, D[5], SC[5]);
  and and_10 (and_10_out, SC[6], D[6]);
  or or_1 (load, p, and_3_out, and_4_out, and_5_out, and_6_out, and_7_out, and_8_out, and_9_out, and_10_out, r_t);

  // Other names for the same wires on the sheet: T2 = SC[2]; T3 = SC[3]; T4 = SC[4]; T5 = SC[5]; T6 = SC[6]
endmodule

module BUS (
  input  [15:0] Memory,
  input  [11:0] AR,
  input  S2,
  input  S0,
  input  S1,
  input  [11:0] PC,
  input  [15:0] DR,
  input  [15:0] AC,
  input  [15:0] IR,
  input  [15:0] TR,
  output [15:0] OUTPUT
);

  Multiplexer #(.select(3), .width(16)) multiplexer_1 (
    .in0({16{1'b0}}), .in1({4'b0000, AR}), .in2({4'b0000, PC}), .in3(DR), .in4(AC), .in5(IR), .in6(TR),
    .in7(Memory), .out(OUTPUT), .sel({S2, S1, S0}));  // open: en

  // Other names for the same wires on the sheet: AR_t[11:0] = AR; PC_t[11:0] = PC
endmodule

module Read_and_Write (
  input  R,
  input  [15:0] SC,
  input  [7:0] D,
  output write,
  output read
);

  wire and_1_out, and_2_out, and_3_out, and_4_out;

  and and_1 (and_1_out, R, SC[1]);
  and and_2 (and_2_out, D[3], SC[4]);
  and and_3 (and_3_out, D[5], SC[4]);
  and and_4 (and_4_out, D[6], SC[6]);
  or or_1 (write, and_1_out, and_2_out, and_3_out, and_4_out);

  assign read = 1'b1;

  // Other names for the same wires on the sheet: T1 = SC[1]; T4 = SC[4]; T6 = SC[6]
endmodule

module BUS_CONTROLLER (
  input  [11:0] Adddress,
  input  [15:0] SC,
  input  R,
  input  I,
  input  [7:0] D,
  output S0,
  output S1,
  output S2
);

  wire and_2_out, and_3_out, and_4_out, and_5_out, and_6_out, and_7_out, and_8_out, and_11_out, and_12_out,
       and_13_out, not_1_out, not_2_out, not_3_out, or_5_out, p, X0, X1, X2, X3, X4, X5, X6, X7;

  and and_1 (p, I, D[7], SC[3]);
  and and_2 (and_2_out, SC[4], D[4]);
  and and_3 (and_3_out, D[5], SC[5]);
  or or_1 (X1, and_2_out, and_3_out);
  or or_2 (X2, SC[0], and_4_out);
  and and_4 (and_4_out, D[5], SC[4]);
  and and_5 (and_5_out, D[6], SC[6]);
  or or_3 (X3, and_5_out, and_6_out);
  and and_6 (and_6_out, D[2], SC[5]);
  and and_7 (and_7_out, Adddress[10], p);
  and and_8 (and_8_out, D[3], SC[4]);
  not not_1 (not_1_out, R);
  and and_9 (X5, not_1_out, SC[2]);
  and and_10 (X6, R, SC[1]);
  or or_4 (X4, and_7_out, and_8_out);
  not not_2 (not_2_out, D[7]);
  not not_3 (not_3_out, R);
  or or_5 (or_5_out, D[0], D[1], D[2], D[6]);
  and and_11 (and_11_out, not_2_out, I, SC[3]);
  and and_12 (and_12_out, SC[1], not_3_out);
  and and_13 (and_13_out, or_5_out, SC[4]);
  Priority_Encoder priority_encoder_1 (
    .in0(X0), .in1(X1), .in2(X2), .in3(X3), .in4(X4), .in5(X5), .in6(X6), .in7(X7), .out({S2, S1, S0}));  // open: en_in, gs, en_out
  nor nor_1 (X0, X1, X2, X3, X4, X5, X6, X7);
  or or_6 (X7, and_11_out, and_12_out, and_13_out);

  // Other names for the same wires on the sheet: B10 = Adddress[10]; T0 = SC[0]; T1 = SC[1]; T2 = SC[2]; T3 = SC[3];
  //   T4 = SC[4]; T5 = SC[5]; T6 = SC[6]
endmodule
